# Fritzing sketch Schema (saved by Fritzing 0.9.3b)
breadboards: 1

parts:
  Part1 = Arduino Uno (Rev3)
  WTV020-SD1 = WTV020-SD [part_number=WTV020-SD]
  Part2 = Real Time Clock Module - DS1307 RTC Breakout Board
  Power_plug1 = Power plug
  IC1 = Voltage Regulator AMS1117 [package=sot223]
  S1 = Round Pushbutton
  LED1 = LED - 5mm [color="Red (633nm)" package="5 mm [THT]"]
  LED2 = LED - 5mm [color="Red (633nm)" package="5 mm [THT]"]
  R1 = Resistor [tolerance=±5% resistance=220 package=THT]

nets:
  N1: Part1.A4/SDA, Part2.SDA
  N2: Part1.A5/SCL, Part2.SCL
  N3: Part1.D4, WTV020-SD1.RESET
  N4: Part1.D5_PWM, WTV020-SD1.P04
  N5: Part1.D6_PWM, WTV020-SD1.P05
  N6: Part1.D7, WTV020-SD1.P06
  5V: Part1.5V, Part2.5V, IC1.IN, S1.leg1, R1.Pin_0
  GND: Part1.GND, Part2.GND, Power_plug1.GND, IC1.GND, LED1.cathode, LED2.cathode
  GND_2: WTV020-SD1.GND, IC1.OUT
  N7: Power_plug1.VCC, S1.leg0
  N8: LED1.anode, LED2.anode, R1.Pin_1
